// Digital circuit HazUnit.dig as structural Verilog
module HazUnit (
  input  [4:0] WR_4,
  input  RFW_4,
  input  [4:0] RR0,
  input  [4:0] WR_3,
  input  RFW_3,
  input  [4:0] RR1,
  input  MLD_3,
  input  PCsel_2,
  output [1:0] FRD0,
  output [1:0] FRD1,
  output CLR_stall,
  output EN_stall,
  output Stall,
  output Flush,
  output CLR_flush
);

  wire and_1_out, and_2_out, and_3_out, and_4_out, and_5_out, comparator_1_eq, comparator_2_eq,
       comparator_3_eq, comparator_4_eq, comparator_5_eq, comparator_6_eq, or_1_out;

  Comparator #(.Bits(5)) comparator_1 (.a(RR0), .b(WR_4), .eq(comparator_1_eq));  // open: gt, lt
  Comparator #(.Bits(5)) comparator_2 (.a(RR0), .b(WR_3), .eq(comparator_2_eq));  // open: gt, lt
  Comparator #(.Bits(5)) comparator_3 (.a(RR1), .b(WR_4), .eq(comparator_3_eq));  // open: gt, lt
  Comparator #(.Bits(5)) comparator_4 (.a(RR1), .b(WR_3), .eq(comparator_4_eq));  // open: gt, lt
  Comparator #(.Bits(5)) comparator_5 (.a(RR0), .b(WR_3), .eq(comparator_5_eq));  // open: gt, lt
  Comparator #(.Bits(5)) comparator_6 (.a(RR1), .b(WR_3), .eq(comparator_6_eq));  // open: gt, lt
  and and_1 (and_1_out, MLD_3, RFW_3);
  Comparator comparator_7 (.a(PCsel_2), .b(1'b1), .eq(CLR_flush));  // open: gt, lt
  and and_2 (and_2_out, comparator_1_eq, RFW_4);
  and and_3 (and_3_out, comparator_2_eq, RFW_3);
  and and_4 (and_4_out, comparator_3_eq, RFW_4);
  and and_5 (and_5_out, comparator_4_eq, RFW_3);
  or or_1 (or_1_out, comparator_5_eq, comparator_6_eq);
  and and_6 (CLR_stall, or_1_out, and_1_out);
  PriorityEncoder #(.Selector_Bits(2)) priorityencoder_1 (
    .in0(1'b1), .in1(and_2_out), .in2(and_3_out), .in3(1'b0), .num(FRD0));  // open: any
  PriorityEncoder #(.Selector_Bits(2)) priorityencoder_2 (
    .in0(1'b1), .in1(and_4_out), .in2(and_5_out), .in3(1'b0), .num(FRD1));  // open: any
  not not_1 (EN_stall, CLR_stall);

  assign Flush = CLR_flush;
  assign Stall = CLR_stall;

  // Other names for the same wires on the sheet: PCsel = PCsel_2; RR0_2[4:0] = RR0; RR1_2[4:0] = RR1
endmodule
